# Fritzing sketch 7led (saved by Fritzing 0.9.2b)
breadboards: 1

parts:
  R3 = Resistor [tolerance=±5% resistance=75 package=THT]
  R5 = Resistor [tolerance=±5% resistance=75 package=THT]
  R6 = Resistor [tolerance=±5% resistance=75 package=THT]
  R7 = Resistor [tolerance=±5% resistance=75 package=THT]
  R8 = Resistor [tolerance=±5% resistance=75 package=THT]
  R9 = Resistor [tolerance=±5% resistance=75 package=THT]
  R4 = Resistor [tolerance=±5% resistance=75 package=THT]
  DI1 = 7-Segment LED Display [package=THT]
  Raspberry_Pi2 = Raspberry Pi 2

nets:
  N1: R3.Pin_0, Raspberry_Pi2.GPIO5
  N2: R3.Pin_1, DI1.cathodeB
  N3: R5.Pin_0, Raspberry_Pi2.GPIO13
  N4: R5.Pin_1, DI1.cathodeF
  N5: R6.Pin_0, Raspberry_Pi2.GPIO19
  N6: R6.Pin_1, DI1.cathodeG
  N7: R7.Pin_0, DI1.cathodeE
  N8: R7.Pin_1, Raspberry_Pi2.GPIO26
  N9: R8.Pin_0, Raspberry_Pi2.GPIO21
  N10: R8.Pin_1, DI1.cathodeD
  N11: R9.Pin_0, DI1.cathodeC
  N12: R9.Pin_1, Raspberry_Pi2.GPIO20
  N13: R4.Pin_0, Raspberry_Pi2.GPIO6
  N14: R4.Pin_1, DI1.cathodeA
  3V3: DI1.commAnode, Raspberry_Pi2.3v3, Raspberry_Pi2.3V3
