# Fritzing sketch hokori (saved by Fritzing 0.9.2b)
breadboards: 1

parts:
  R1 = Resistor [tolerance=±5% resistance=150 package=THT]
  IC1 = IC, DIP package, 6 pins [chip_label=3425]
  R3 = Resistor [tolerance=±5% resistance=100 package=THT]
  R5 = Resistor [tolerance=±5% resistance=100 package=THT]
  R6 = Resistor [tolerance=±5% resistance=100 package=THT]
  R7 = Resistor [tolerance=±5% resistance=100 package=THT]
  R8 = Resistor [tolerance=±5% resistance=100 package=THT]
  R9 = Resistor [tolerance=±5% resistance=100 package=THT]
  GP2Y1010AU = Header 6 [package=em406]
  R2 = Resistor [tolerance=±5% resistance=10k package=THT]
  R4 = Resistor [tolerance=±5% resistance=100 package=THT]
  Q1 = NPN-Transistor [part_number=1815 package="TO92 [THT]"]
  C1 = Electrolytic Capacitor [capacitance=0.22mF voltage=6.3V package="1010 [SMD, electrolytic]"]
  Raspberry_Pi2 = Raspberry Pi 2
  R10 = Resistor [tolerance=±5% resistance=10k package=THT]
  S1 = Pushbutton [package="[THT]"]
  DI1 = 7-Segment LED Display [package=THT]

nets:
  N1: R1.Pin_0, GP2Y1010AU.1, C1.+
  N2: R1.Pin_1, GP2Y1010AU.6, Raspberry_Pi2.5V
  N3: IC1.pin1, GP2Y1010AU.5
  N4: IC1.pin2, GP2Y1010AU.2, GP2Y1010AU.4, Q1.E, C1.-, Raspberry_Pi2.GND, S1.Pin_1, S1.Pin_2
  N5: IC1.pin3, Raspberry_Pi2.GPIO3
  N6: IC1.pin4, Raspberry_Pi2.GPIO2
  3V3: IC1.pin5, IC1.pin6, Raspberry_Pi2.3v3, Raspberry_Pi2.3V3, R10.Pin_1, DI1.commAnode#2
  N7: R3.Pin_0, Raspberry_Pi2.GPIO5
  N8: R3.Pin_1, DI1.cathodeB
  N9: R5.Pin_0, Raspberry_Pi2.GPIO13
  N10: R5.Pin_1, DI1.cathodeF
  N11: R6.Pin_0, Raspberry_Pi2.GPIO19
  N12: R6.Pin_1, DI1.cathodeG
  N13: R7.Pin_0, DI1.cathodeE
  N14: R7.Pin_1, Raspberry_Pi2.GPIO26
  N15: R8.Pin_0, Raspberry_Pi2.GPIO21
  N16: R8.Pin_1, DI1.cathodeD
  N17: R9.Pin_0, DI1.cathodeC
  N18: R9.Pin_1, Raspberry_Pi2.GPIO20
  N19: GP2Y1010AU.3, Q1.C
  N20: R2.Pin_0, Raspberry_Pi2.GPIO18
  N21: R2.Pin_1, Q1.B
  N22: R4.Pin_0, Raspberry_Pi2.GPIO6
  N23: R4.Pin_1, DI1.cathodeA
  N24: Raspberry_Pi2.GPIO16, R10.Pin_0, S1.Pin_3, S1.Pin_4
