# Fritzing sketch sensor (saved by Fritzing 0.9.2b)
breadboards: 1

parts:
  R1 = Resistor [tolerance=±5% resistance=150 package=THT]
  MCP3425 = IC, DIP package, 6 pins [chip_label=3425]
  GP2Y1010AU = Header 6 [package=em406]
  R2 = Resistor [tolerance=±5% resistance=10k package=THT]
  Q1 = NPN-Transistor [part_number=1815 package="TO92 [THT]"]
  C1 = Electrolytic Capacitor [capacitance=0.22mF voltage=6.3V package="1010 [SMD, electrolytic]"]
  Raspberry_Pi2 = Raspberry Pi 2

nets:
  N1: R1.Pin_0, GP2Y1010AU.1, C1.+
  N2: R1.Pin_1, GP2Y1010AU.6, Raspberry_Pi2.5V
  N3: MCP3425.pin1, GP2Y1010AU.5
  N4: MCP3425.pin2, GP2Y1010AU.2, GP2Y1010AU.4, Q1.E, C1.-, Raspberry_Pi2.GND
  N5: MCP3425.pin3, Raspberry_Pi2.GPIO3
  N6: MCP3425.pin4, Raspberry_Pi2.GPIO2
  3V3: MCP3425.pin5, MCP3425.pin6, Raspberry_Pi2.3v3, Raspberry_Pi2.3V3
  N7: GP2Y1010AU.3, Q1.C
  N8: R2.Pin_0, Raspberry_Pi2.GPIO18
  N9: R2.Pin_1, Q1.B
